// Logisim project cpuproj.circ as structural Verilog: 1 circuit, main circuit main
module main (
  output [7:0] RegData1,
  output [7:0] ReadDataM,
  output [7:0] RegData2,
  output [7:0] RegDataW
);

  wire and_1_out, and_2_out, and_3_out, and_4_out, and_5_out, decoder_1_out0, decoder_1_out1, decoder_1_out2,
       decoder_1_out3, not_1_out, not_2_out, not_3_out, or_1_out, or_2_out, TheClock_out, xor_1_out;
  wire [1:0] InstructionFetching_dout_2, multiplexer_1_out;
  wire [7:0] adder_1_out, adder_2_out, multiplexer_4_out, multiplexer_5_out, PC_q, subtractor_1_out, X0_q,
       X1_q, X2_q, X3_q;
  wire [7:2] InstructionFetching_dout;

  Clock TheClock (.out(TheClock_out));
  Register PC (.D(adder_1_out), .en(1'b1), .clk(TheClock_out), .Q(PC_q));  // open: clr
  RAM #(.enables("line")) InstructionFetching (
    .addr(PC_q), .clk(TheClock_out), .dout({InstructionFetching_dout, InstructionFetching_dout_2}));  // open: we, din
  Adder adder_1 (.a(PC_q), .b(8'h1), .out(adder_1_out));  // open: cin, cout
  LED led_1 (.in(TheClock_out));
  LED led_2 (.in(TheClock_out));
  LED led_3 (.in(TheClock_out));
  LED led_4 (.in(TheClock_out));
  LED led_5 (.in(TheClock_out));
  LED led_6 (.in(TheClock_out));
  LED led_7 (.in(TheClock_out));
  LED led_8 (.in(TheClock_out));
  LED led_9 (.in(TheClock_out));
  LED led_10 (.in(TheClock_out));
  LED led_11 (.in(TheClock_out));
  LED led_12 (.in(TheClock_out));
  LED led_13 (.in(TheClock_out));
  LED led_14 (.in(TheClock_out));
  LED led_15 (.in(TheClock_out));
  LED led_16 (.in(TheClock_out));
  LED led_17 (.in(TheClock_out));
  LED led_18 (.in(TheClock_out));
  LED led_19 (.in(TheClock_out));
  LED led_20 (.in(TheClock_out));
  LED led_21 (.in(TheClock_out));
  LED led_22 (.in(TheClock_out));
  LED led_23 (.in(TheClock_out));
  LED led_24 (.in(TheClock_out));
  LED led_25 (.in(TheClock_out));
  LED led_26 (.in(TheClock_out));
  LED led_27 (.in(TheClock_out));
  LED led_28 (.in(TheClock_out));
  LED led_29 (.in(TheClock_out));
  LED led_30 (.in(TheClock_out));
  LED led_31 (.in(TheClock_out));
  LED led_32 (.in(TheClock_out));
  LED led_33 (.in(TheClock_out));
  LED led_34 (.in(TheClock_out));
  LED led_35 (.in(TheClock_out));
  LED led_36 (.in(TheClock_out));
  LED led_37 (.in(TheClock_out));
  LED led_38 (.in(TheClock_out));
  LED led_39 (.in(TheClock_out));
  LED led_40 (.in(TheClock_out));
  LED led_41 (.in(TheClock_out));
  LED led_42 (.in(TheClock_out));
  LED led_43 (.in(TheClock_out));
  LED led_44 (.in(TheClock_out));
  LED led_45 (.in(TheClock_out));
  LED led_46 (.in(TheClock_out));
  LED led_47 (.in(TheClock_out));
  LED led_48 (.in(TheClock_out));
  LED led_49 (.in(TheClock_out));
  not not_1 (not_1_out, InstructionFetching_dout[7]);
  xor xor_1 (xor_1_out, InstructionFetching_dout[6], InstructionFetching_dout[7]);
  or or_1 (or_1_out, InstructionFetching_dout[6], InstructionFetching_dout[7]);
  LED led_50 (.in(TheClock_out));
  LED led_51 (.in(TheClock_out));
  LED led_52 (.in(TheClock_out));
  LED led_53 (.in(TheClock_out));
  LED led_54 (.in(TheClock_out));
  LED led_55 (.in(TheClock_out));
  LED led_56 (.in(TheClock_out));
  LED led_57 (.in(TheClock_out));
  LED led_58 (.in(TheClock_out));
  LED led_59 (.in(TheClock_out));
  LED led_60 (.in(TheClock_out));
  LED led_61 (.in(TheClock_out));
  LED led_62 (.in(TheClock_out));
  LED led_63 (.in(TheClock_out));
  or or_2 (or_2_out, InstructionFetching_dout[6], not_1_out);
  // RGBLED rgbled_1: pin names not known; wires that end beside it: TheClock_out, TheClock_out, TheClock_out
  // RGBLED rgbled_2: pin names not known; wires that end beside it: TheClock_out
  // RGBLED rgbled_3: pin names not known; wires that end beside it: TheClock_out
  LED led_64 (.in(TheClock_out));
  // RGBLED rgbled_4: pin names not known; wires that end beside it: TheClock_out
  LED led_65 (.in(TheClock_out));
  // RGBLED rgbled_5: pin names not known; wires that end beside it: TheClock_out
  LED led_66 (.in(TheClock_out));
  // RGBLED rgbled_6: pin names not known
  Multiplexer #(.width(2)) multiplexer_1 (
    .in0(InstructionFetching_dout_2), .in1(InstructionFetching_dout[5:4]), .out(multiplexer_1_out),
    .sel(xor_1_out));
  LED led_67 (.in(TheClock_out));
  LED led_68 (.in(TheClock_out));
  LED led_69 (.in(TheClock_out));
  LED led_70 (.in(TheClock_out));
  LED led_71 (.in(TheClock_out));
  LED led_72 (.in(TheClock_out));
  LED led_73 (.in(TheClock_out));
  LED led_74 (.in(TheClock_out));
  LED led_75 (.in(TheClock_out));
  LED led_76 (.in(TheClock_out));
  LED led_77 (.in(TheClock_out));
  LED led_78 (.in(TheClock_out));
  LED led_79 (.in(TheClock_out));
  LED led_80 (.in(TheClock_out));
  LED led_81 (.in(TheClock_out));
  LED led_82 (.in(TheClock_out));
  LED led_83 (.in(TheClock_out));
  LED led_84 (.in(TheClock_out));
  LED led_85 (.in(TheClock_out));
  LED led_86 (.in(TheClock_out));
  LED led_87 (.in(TheClock_out));
  LED led_88 (.in(TheClock_out));
  LED led_89 (.in(TheClock_out));
  LED led_90 (.in(TheClock_out));
  Decoder #(.select(2)) decoder_1 (
    .out0(decoder_1_out0), .out1(decoder_1_out1), .out2(decoder_1_out2), .out3(decoder_1_out3),
    .sel(multiplexer_1_out));  // open: en
  and and_1 (and_1_out, InstructionFetching_dout[7], xor_1_out);
  not not_2 (not_2_out, xor_1_out);
  LED led_91 (.in(TheClock_out));
  LED led_92 (.in(TheClock_out));
  LED led_93 (.in(TheClock_out));
  LED led_94 (.in(TheClock_out));
  LED led_95 (.in(TheClock_out));
  LED led_96 (.in(TheClock_out));
  LED led_97 (.in(TheClock_out));
  LED led_98 (.in(TheClock_out));
  LED led_99 (.in(TheClock_out));
  LED led_100 (.in(TheClock_out));
  LED led_101 (.in(TheClock_out));
  and and_2 (and_2_out, or_2_out, decoder_1_out0);
  and and_3 (and_3_out, or_2_out, decoder_1_out1);
  and and_4 (and_4_out, or_2_out, decoder_1_out2);
  and and_5 (and_5_out, or_2_out, decoder_1_out3);
  LED led_102 (.in(TheClock_out));
  LED led_103 (.in(TheClock_out));
  LED led_104 (.in(TheClock_out));
  LED led_105 (.in(TheClock_out));
  LED led_106 (.in(TheClock_out));
  LED led_107 (.in(TheClock_out));
  LED led_108 (.in(TheClock_out));
  LED led_109 (.in(TheClock_out));
  LED led_110 (.in(TheClock_out));
  Register X0 (.D(RegDataW), .en(and_2_out), .clk(TheClock_out), .Q(X0_q));  // open: clr
  Register X1 (.D(RegDataW), .en(and_3_out), .clk(TheClock_out), .Q(X1_q));  // open: clr
  Register X2 (.D(RegDataW), .en(and_4_out), .clk(TheClock_out), .Q(X2_q));  // open: clr
  Register X3 (.D(RegDataW), .en(and_5_out), .clk(TheClock_out), .Q(X3_q));  // open: clr
  LED led_111 (.in(TheClock_out));
  LED led_112 (.in(TheClock_out));
  LED led_113 (.in(TheClock_out));
  LED led_114 (.in(TheClock_out));
  LED led_115 (.in(TheClock_out));
  LED led_116 (.in(TheClock_out));
  LED led_117 (.in(TheClock_out));
  LED led_118 (.in(TheClock_out));
  LED led_119 (.in(TheClock_out));
  LED led_120 (.in(TheClock_out));
  LED led_121 (.in(TheClock_out));
  LED led_122 (.in(TheClock_out));
  LED led_123 (.in(TheClock_out));
  LED led_124 (.in(TheClock_out));
  LED led_125 (.in(TheClock_out));
  LED led_126 (.in(TheClock_out));
  LED led_127 (.in(TheClock_out));
  LED led_128 (.in(TheClock_out));
  LED led_129 (.in(TheClock_out));
  LED led_130 (.in(TheClock_out));
  LED led_131 (.in(TheClock_out));
  LED led_132 (.in(TheClock_out));
  LED led_133 (.in(TheClock_out));
  LED led_134 (.in(TheClock_out));
  LED led_135 (.in(TheClock_out));
  LED led_136 (.in(TheClock_out));
  LED led_137 (.in(TheClock_out));
  LED led_138 (.in(TheClock_out));
  LED led_139 (.in(TheClock_out));
  LED led_140 (.in(TheClock_out));
  LED led_141 (.in(TheClock_out));
  LED led_142 (.in(TheClock_out));
  LED led_143 (.in(TheClock_out));
  Multiplexer #(.select(2), .width(8)) multiplexer_2 (
    .in0(X0_q), .in1(X1_q), .in2(X2_q), .in3(X3_q), .out(RegData1), .sel(InstructionFetching_dout[5:4]));
  Multiplexer #(.select(2), .width(8)) multiplexer_3 (
    .in0(X0_q), .in1(X1_q), .in2(X2_q), .in3(X3_q), .out(RegData2), .sel(InstructionFetching_dout[3:2]));
  LED led_144 (.in(TheClock_out));
  LED led_145 (.in(TheClock_out));
  LED led_146 (.in(TheClock_out));
  LED led_147 (.in(TheClock_out));
  LED led_148 (.in(TheClock_out));
  LED led_149 (.in(TheClock_out));
  LED led_150 (.in(TheClock_out));
  LED led_151 (.in(TheClock_out));
  LED led_152 (.in(TheClock_out));
  LED led_153 (.in(TheClock_out));
  LED led_154 (.in(TheClock_out));
  LED led_155 (.in(TheClock_out));
  LED led_156 (.in(TheClock_out));
  LED led_157 (.in(TheClock_out));
  LED led_158 (.in(TheClock_out));
  Multiplexer #(.width(8)) multiplexer_4 (
    .in0(RegData1), .in1({{6{1'b0}}, InstructionFetching_dout_2}), .out(multiplexer_4_out), .sel(xor_1_out));
  Adder adder_2 (.a(multiplexer_4_out), .b(RegData2), .out(adder_2_out));  // open: cin, cout
  Subtractor subtractor_1 (.a(RegData1), .b(RegData2), .out(subtractor_1_out));  // open: bin, bout
  not not_3 (not_3_out, or_1_out);
  Multiplexer #(.width(8)) multiplexer_5 (
    .in0(adder_2_out), .in1(subtractor_1_out), .out(multiplexer_5_out), .sel(not_3_out));
  RAM #(.enables("line")) Memory (
    .addr(multiplexer_5_out), .we(and_1_out), .clk(TheClock_out), .din(RegData1), .dout(ReadDataM));
  Multiplexer #(.width(8)) multiplexer_6 (.in0(ReadDataM), .in1(multiplexer_5_out), .out(RegDataW), .sel(not_2_out));

  // Notes on the sheet:
  //   Alvaro Izquierdo 
  //   if its 00 then the output is 0 otherwise its 1 which allows to choose between ADD or SUB in ALU ->
  //   I pledge my honor that I have abided by the Stevens Honor System
  //   imm/destreg
  //   if 01 or 10 then the output is 1 which allows to choose the imm ->
  //   Adithya Ganesh
  //   Reg 2
  //   Reg1
  //   Opcode
  //   writeenable (only on for LDUR/ADD/SUB)
  //   Chooses WriteReg based off Opcode
  //   Register File
  //   turns write enable on/off depending on LDUR(01) or STUR(10)
  //   ReadReg1
  //   ReadReg2
  //   pading 0's so 2 bit imm can be 8 bit
  //   Chooses between Reg1Data or Imm
  //   ALU
  //   <- Choose immediate if LDUR or STUR
  //   Chooses between ADD/SUB
  //   Chooses between the data read in the memory or the ALUout
endmodule
